# Fritzing sketch Otopark_projesi (saved by Fritzing 0.9.3b)
breadboards: 1

parts:
  Part1 = Arduino Uno (Rev3)
  hc-sr1 = hc-sr04
  hc-sr2 = hc-sr04
  J2 = Basic Servo
  J1 = Basic Servo
  LCM1602_IIC1 = LCM1602 IIC [part_number="LCM1602 IIC" chip_label="LCM1602 IIC" package="DIP (Dual Inline) [THT]"]

nets:
  N1: Part1.A4/SDA, LCM1602_IIC1.SDA
  N2: Part1.A5/SCL, LCM1602_IIC1.SCL
  N3: Part1.D8, J2.pulse
  N4: Part1.D9_PWM, J1.pulse
  GND: Part1.GND, hc-sr1.GND, hc-sr2.GND, J2.gnd, J1.gnd, LCM1602_IIC1.GND
  N5: Part1.D2, hc-sr1.Trig
  N6: Part1.D3_PWM, hc-sr1.Echo
  N7: Part1.D4, hc-sr2.Trig
  N8: Part1.D5_PWM, hc-sr2.Echo
  VCC: Part1.5V, hc-sr1.VCC, hc-sr2.VCC, J2.vcc, J1.vcc, LCM1602_IIC1.VCC

notes:
  Akıllı Otopark Projesi
  Ugur Enes UZUN

custom parts:
  LCM1602 IIC: I2C-Module to use a 1602 or 2004 LCD on with the wire.h libory Serial LCD Modul
